# Fritzing sketch main (saved by Fritzing 0.9.3b)
breadboards: 1

parts:
  Raspberry_Pi_Zero1 = Raspberry Pi Zero
  part = Barometric Pressure Sensor - BMP180 Breakout (GY-68)
  part_2 = IC, DIP package, 16 pins [chip_label=PCF8591]
  o1 = Module display OLED I2C 128x64 SSD1306 [package=THT]
  ZS-042_RTC1 = ZS-042 RTC Module
  S1 = Round Pushbutton  # not connected
  S2 = Round Pushbutton  # not connected
  LED1 = smd LED [color="Green (565nm)" package="1206 [SMD]"]
  LED2 = smd LED [color="Blue (505nm)" package="1206 [SMD]"]
  ULN2803 = Darlington Driver [package=dil18]
  R1 = Resistor [tolerance=±5% resistance=220 package=THT]
  R2 = Resistor [tolerance=±5% resistance=220 package=THT]

nets:
  VCC: Raspberry_Pi_Zero1.3v3, Raspberry_Pi_Zero1.3V3, part.VCC, part_2.pin14, part_2.pin16, o1.VCC, ZS-042_RTC1.VCC
  N1: Raspberry_Pi_Zero1.GPIO2, part.SDA, part_2.pin9, o1.SDA, ZS-042_RTC1.SDA
  N2: Raspberry_Pi_Zero1.GPIO3, part.SCL, part_2.pin10, o1.SCL, ZS-042_RTC1.SCL
  GND: Raspberry_Pi_Zero1.GND, part.GND, part_2.pin2, part_2.pin3, part_2.pin4, part_2.pin5, part_2.pin6, part_2.pin7, part_2.pin8, part_2.pin12, o1.GND, ZS-042_RTC1.GND, ULN2803.9
  N3: Raspberry_Pi_Zero1.5V, LED1.anode, LED2.anode
  N4: LED1.cathode, R2.Pin_0
  N5: LED2.cathode, R1.Pin_0
  N6: ULN2803.17, R1.Pin_1
  N7: ULN2803.18, R2.Pin_1

custom parts:
  Module display OLED I2C 128x64 SSD1306: Ecran OLED I2C SSD163 de 128x64 avec connexion I2C
