# Fritzing sketch powersupply (saved by Fritzing 0.9.3b)
circuit board: 8.46667cm x 5.64444cm
breadboards: 1

parts:
  C1 = Tantalum Capacitor [capacitance=47µF voltage=10V package="100 mil [THT, tantalum]"]
  R1 = Resistor [tolerance=±1% resistance=3.3M package=THT]
  U1 = 556 [package=dil14]
  D1 = Rectifier Diode [part_number=1N4001 package="300 mil [THT]"]
  D2 = Rectifier Diode [part_number=1N4001 package="300 mil [THT]"]
  Q1 = NPN-Transistor [package="TO92 [THT]"]
  C2 = Tantalum Capacitor [capacitance=47µF voltage=10V package="100 mil [THT, tantalum]"]
  R2 = Resistor [tolerance=±1% resistance=100 package=THT]
  R3 = Resistor [tolerance=±1% resistance=3.3M package=THT]
  R4 = Resistor [tolerance=±1% resistance=100 package=THT]
  S1 = Square Pushbutton
  R5 = Resistor [tolerance=±1% resistance=10k package=THT]
  R6 = Resistor [tolerance=±1% resistance=10k package=THT]
  Q2 = MOSFET-NCHANNEL [package=to220v]
  part = RioRand LM2596
  JP1 = Header 4 [package=jst-4-pth]

nets:
  GND: C1.-, U1.GND, Q1.E, C2.-, S1.leg0, R6.Pin_0, Q2.S
  N1: C1.+, R1.Pin_0, U1.THR, U1.TRIG, R2.Pin_1
  9V: R1.Pin_1, U1.RST, U1.RST2, U1.VCC, R3.Pin_1, part.Pin_0, JP1.2
  N2: U1.OUT, D1.anode
  N3: U1.TRIG2, U1.THR2, C2.+, R3.Pin_0, R4.Pin_0
  N4: U1.OUT2, D2.anode
  N5: D1.cathode, D2.cathode, R6.Pin_1, Q2.G
  N6: Q1.B, R5.Pin_1
  N7: Q1.C, R2.Pin_0
  N8: R4.Pin_1, S1.leg1
  N9: R5.Pin_0, JP1.1
  N10: Q2.D, part.Pin_1
  N11: part.Pin_2, JP1.3
  N12: part.Pin_3, JP1.4

notes:
  +5 V Power Supply for Raspberry Pi
  Voltage Control
  Raspi Pin #??
